# Fritzing sketch Untitled Sketch 2 (saved by Fritzing 0.9.9b)
breadboards: 1

parts:
  S1 = Pushbutton [package="[THT]"]
  R1 = Resistor [tolerance=±5% power=0.25 resistance=220 package=THT]
  LED1 = LED - 5mm [color="Blue (430nm)" current=0.030 package="5 mm [THT]"]
  Componente1 = Arduino Uno (Rev3)
  R2 = Resistor [tolerance=±5% power=0.25 resistance=220 package=THT]
  LED2 = LED - 5mm [color="White (4500K)" current=0.030 package="5 mm [THT]"]
  S2 = Pushbutton [package="[THT]"]
  R3 = Resistor [tolerance=±5% power=0.25 resistance=220 package=THT]

nets:
  N1: S1.Pin_1, S1.Pin_2, Componente1.5V
  N2: S1.Pin_3, S1.Pin_4, Componente1.D2, R2.Pin_1
  N3: R1.Pin_0, Componente1.GND, R2.Pin_0, R3.Pin_0
  N4: R1.Pin_1, LED1.cathode, LED2.cathode
  N5: LED1.anode, Componente1.D13/SCK, LED2.anode
  N6: Componente1.D1/TX, S2.Pin_1, S2.Pin_2
  N7: S2.Pin_3, S2.Pin_4, R3.Pin_1
