# Fritzing sketch Untitled Sketch 3 (saved by Fritzing 0.9.9b)
breadboards: 1

parts:
  Componente1 = Arduino Uno (Rev3)
  R1 = Resistor [tolerance=±5% power=0.25 resistance=220 package=THT]
  R2 = Rotary Potentiometer (Small) [maximum_resistance=100kΩ package=THT]
  LED1 = LED - 5mm [color="Blue (430nm)" current=0.030 package="5 mm [THT]"]

nets:
  N1: Componente1.A2, R2.wiper
  N2: Componente1.D13/SCK, LED1.cathode
  N3: Componente1.5V, R2.leg2
  N4: Componente1.GND, R1.Pin_1, R2.leg1
  N5: R1.Pin_0, LED1.anode
