# Fritzing sketch Untitled Sketch (saved by Fritzing 0.9.9b)
breadboards: 1

parts:
  R2 = Resistor [tolerance=±5% power=0.25 resistance=220 package=THT]
  Componente1 = Arduino Ethernet Shield (Rev3)
  M1 = DC Motor
  LED1 = LED - 5mm [color="Blue (430nm)" current=0.030 package="5 mm [THT]"]
  HC-SR04_Sensor_1 = HC-SR04 Ultrasonic Distance Sensor

nets:
  N1: R2.Pin_0, Componente1.SDCS, LED1.anode
  GND: R2.Pin_1, Componente1.GND, M1.pin_2, HC-SR04_Sensor_1.GND
  N2: Componente1.SPI/D12, M1.pin_1
  N3: Componente1.PWM_D5, HC-SR04_Sensor_1.ECHO
  N4: Componente1.PWM_D6, HC-SR04_Sensor_1.TRIG
  3V3: Componente1.3V3, HC-SR04_Sensor_1.VCC
