# Fritzing sketch Untitled Sketch (saved by Fritzing 0.9.9b)
breadboards: 1

parts:
  R1 = Resistor [tolerance=±5% power=0.25 resistance=220 package=THT]
  R2 = Resistor [tolerance=±5% power=0.25 resistance=220 package=THT]
  LED1 = LED - 5mm [color="Red (633nm)" current=0.030 package="5 mm [THT]"]
  Componente1 = Arduino Ethernet Shield (Rev3)
  M1 = DC Motor
  S1 = Pushbutton [package="[THT]"]

nets:
  N1: R1.Pin_0, LED1.cathode, Componente1.GND, M1.pin_2
  N2: R1.Pin_1, Componente1.D2, S1.Pin_3, S1.Pin_4
  N3: R2.Pin_1, Componente1.D8
  N4: Componente1.PWM_D5, M1.pin_1
  N5: Componente1.5V, S1.Pin_1, S1.Pin_2
